// Logisim project parte1_cache.circ as structural Verilog: 5 circuits, main circuit main
module main (
  input  [7:0] Base,
  input  [7:0] Deslocamento,
  input  Clock,
  input  Zerar
);

  wire cache_1_acerto;
  wire [7:0] adder_1_out;

  Adder adder_1 (.a(Base), .b(Deslocamento), .out(adder_1_out), .cin(1'b0));  // open: cout
  // Probe on adder_1_out[5:0]
  LED led_1 (.in(cache_1_acerto));
  cache cache_1 (.Endereco(adder_1_out[5:0]), .clock(Clock), .zerar(Zerar), .Acesso(1'b1), .acerto(cache_1_acerto));
endmodule

module cache (
  input  [5:0] Endereco,
  input  clock,
  input  zerar,
  input  Acesso,
  output acerto
);

  wire and_5_out, and_6_out, and_7_out, and_8_out, and_9_out, and_10_out, and_11_out, decoder_1_out0,
       decoder_1_out1, decoder_1_out2, decoder_1_out3, decodificador_7segmentos_1_a,
       decodificador_7segmentos_1_b, decodificador_7segmentos_1_c, decodificador_7segmentos_1_d,
       decodificador_7segmentos_1_e, decodificador_7segmentos_1_f, decodificador_7segmentos_1_g, Falha_L0,
       Falha_L1, Falha_L2, Falha_L3, multiplexer_2_out, not_1_out, not_2_out, not_3_out, not_4_out,
       not_5_out, not_6_out, not_7_out, not_8_out, not_9_out, not_10_out, not_11_out, or_1_out, or_2_out,
       or_3_out, or_4_out, Valido_L0_q, Valido_L1_q, Valido_L2_q, Valido_L3_q;
  wire [2:0] multiplexer_1_out, Rotulo_L0_q, Rotulo_L1_q, Rotulo_L2_q, Rotulo_L3_q;
  wire [3:0] counter_1_q;

  Decoder #(.select(2)) decoder_1 (
    .out0(decoder_1_out0), .out1(decoder_1_out1), .out2(decoder_1_out2), .out3(decoder_1_out3),
    .sel(Endereco[2:1]), .en(1'b1));
  not not_1 (not_1_out, acerto);
  not not_2 (not_2_out, acerto);
  not not_3 (not_3_out, acerto);
  not not_4 (not_4_out, acerto);
  and and_1 (Falha_L0, decoder_1_out0, Acesso, not_1_out);
  and and_2 (Falha_L1, decoder_1_out1, Acesso, not_2_out);
  and and_3 (Falha_L2, decoder_1_out2, Acesso, not_3_out);
  and and_4 (Falha_L3, decoder_1_out3, Acesso, not_4_out);
  Register #(.width(3)) Rotulo_L0 (.D(Endereco[5:3]), .en(Falha_L0), .clk(clock), .Q(Rotulo_L0_q), .clr(zerar));
  and and_5 (and_5_out, acerto, Acesso);
  Counter #(.max('hf), .width(4)) counter_1 (
    .clr(zerar), .load(1'b0), .up(1'b1), .count(and_5_out), .clk(clock), .Q(counter_1_q));  // open: D, carry
  J_K_Flip_Flop Valido_L0 (.J(Falha_L0), .K(1'b0), .clk(clock), .Q(Valido_L0_q), .reset(zerar));  // open: Qn, preset
  Register #(.width(3)) Rotulo_L1 (.D(Endereco[5:3]), .en(Falha_L1), .clk(clock), .Q(Rotulo_L1_q), .clr(zerar));
  J_K_Flip_Flop Valido_L1 (.J(Falha_L1), .K(1'b0), .clk(clock), .Q(Valido_L1_q), .reset(zerar));  // open: Qn, preset
  Register #(.width(3)) Rotulo_L2 (.D(Endereco[5:3]), .en(Falha_L2), .clk(clock), .Q(Rotulo_L2_q), .clr(zerar));
  Decodificador_7segmentos decodificador_7segmentos_1 (
    .Contador(counter_1_q), .a(decodificador_7segmentos_1_a), .b(decodificador_7segmentos_1_b),
    .c(decodificador_7segmentos_1_c), .d(decodificador_7segmentos_1_d), .e(decodificador_7segmentos_1_e),
    .f(decodificador_7segmentos_1_f), .g(decodificador_7segmentos_1_g));
  J_K_Flip_Flop Valido_L2 (.J(Falha_L2), .K(1'b0), .clk(clock), .Q(Valido_L2_q), .reset(zerar));  // open: Qn, preset
  _7_Segment_Display u_7_segment_display_1 (
    .g(decodificador_7segmentos_1_g), .f(decodificador_7segmentos_1_f), .a(decodificador_7segmentos_1_a),
    .b(decodificador_7segmentos_1_b), .e(decodificador_7segmentos_1_e), .d(decodificador_7segmentos_1_d),
    .c(decodificador_7segmentos_1_c));  // open: dp
  Register #(.width(3)) Rotulo_L3 (.D(Endereco[5:3]), .en(Falha_L3), .clk(clock), .Q(Rotulo_L3_q), .clr(zerar));
  J_K_Flip_Flop Valido_L3 (.J(Falha_L3), .K(1'b0), .clk(clock), .Q(Valido_L3_q), .reset(zerar));  // open: Qn, preset
  Multiplexer #(.select(2), .width(3)) multiplexer_1 (
    .in0(Rotulo_L0_q), .in1(Rotulo_L1_q), .in2(Rotulo_L2_q), .in3(Rotulo_L3_q), .out(multiplexer_1_out),
    .sel(Endereco[2:1]));
  Multiplexer #(.select(2)) multiplexer_2 (
    .in0(Valido_L0_q), .in1(Valido_L1_q), .in2(Valido_L2_q), .in3(Valido_L3_q), .out(multiplexer_2_out),
    .sel(Endereco[2:1]));
  not not_5 (not_5_out, Endereco[5]);
  not not_6 (not_6_out, multiplexer_1_out[2]);
  not not_7 (not_7_out, Endereco[4]);
  not not_8 (not_8_out, multiplexer_1_out[1]);
  not not_9 (not_9_out, Endereco[3]);
  not not_10 (not_10_out, multiplexer_1_out[0]);
  and and_6 (and_6_out, not_5_out, multiplexer_1_out[2]);
  and and_7 (and_7_out, Endereco[5], not_6_out);
  and and_8 (and_8_out, not_7_out, multiplexer_1_out[1]);
  and and_9 (and_9_out, Endereco[4], not_8_out);
  and and_10 (and_10_out, not_9_out, multiplexer_1_out[0]);
  and and_11 (and_11_out, Endereco[3], not_10_out);
  or or_1 (or_1_out, and_8_out, and_9_out);
  or or_2 (or_2_out, and_10_out, and_11_out);
  or or_3 (or_3_out, and_6_out, and_7_out);
  or or_4 (or_4_out, or_3_out, or_1_out, or_2_out);
  not not_11 (not_11_out, or_4_out);
  and and_12 (acerto, not_11_out, multiplexer_2_out);

  // Other names for the same wires on the sheet: Indice[1:0] = Endereco[2:1]
endmodule

module Decodificador_7segmentos (
  input  [3:0] Contador,
  output a,
  output b,
  output c,
  output d,
  output e,
  output f,
  output g
);

  wire cinco_out, dois_out, not_1_out, not_2_out, not_3_out, not_4_out, oito_out, quatro_out, seis_out,
       sete_out, tres_out, um_out, zero_out;

  not not_1 (not_1_out, Contador[3]);
  not not_2 (not_2_out, Contador[2]);
  not not_3 (not_3_out, Contador[1]);
  not not_4 (not_4_out, Contador[0]);
  and zero (zero_out, not_1_out, not_2_out, not_3_out, not_4_out);
  and um (um_out, not_1_out, not_2_out, not_3_out, Contador[0]);
  and dois (dois_out, not_1_out, not_2_out, Contador[1], not_4_out);
  and tres (tres_out, not_1_out, not_2_out, Contador[1], Contador[0]);
  and quatro (quatro_out, not_1_out, Contador[2], not_3_out, not_4_out);
  and cinco (cinco_out, not_1_out, Contador[2], not_3_out, Contador[0]);
  and seis (seis_out, not_1_out, Contador[2], Contador[1], not_4_out);
  and sete (sete_out, not_1_out, Contador[2], Contador[1], Contador[0]);
  and oito (oito_out, Contador[3], not_2_out, not_3_out, not_4_out);
  or or_1 (a, zero_out, dois_out, tres_out, cinco_out, seis_out, sete_out, oito_out);
  or or_2 (b, zero_out, um_out, dois_out, tres_out, quatro_out, sete_out, oito_out);
  or or_3 (c, zero_out, um_out, tres_out, quatro_out, cinco_out, seis_out, sete_out, oito_out);
  or or_4 (d, zero_out, dois_out, tres_out, cinco_out, seis_out, oito_out);
  or or_5 (e, zero_out, dois_out, seis_out, oito_out);
  or or_6 (f, zero_out, quatro_out, cinco_out, seis_out, oito_out);
  or or_7 (g, dois_out, tres_out, quatro_out, cinco_out, seis_out, oito_out);
endmodule

module ConflitoPrimos (
  input  Clear,
  input  Clock
);

  wire Acesso, cache_1_acerto;
  wire [2:0] counter_1_q;

  Counter #(.max('h7), .width(3)) counter_1 (
    .clr(Clear), .load(1'b0), .up(1'b1), .count(1'b1), .clk(Clock), .Q(counter_1_q));  // open: D, carry
  DetectorPrimos detectorprimos_1 (
    .A(1'b0), .B(counter_1_q[2]), .C(counter_1_q[1]), .D(counter_1_q[0]), .Primo(Acesso));
  LED led_1 (.in(Acesso));
  LED led_2 (.in(cache_1_acerto));
  cache cache_1 (
    .Endereco({counter_1_q, 3'b000}), .clock(Clock), .zerar(Clear), .Acesso(Acesso), .acerto(cache_1_acerto));
endmodule

module DetectorPrimos (
  input  A,
  input  B,
  input  C,
  input  D,
  output Primo
);

  wire cincosete_out, doistres_out, not_1_out, not_2_out, not_3_out, onze_out, treze_out;

  not not_1 (not_1_out, A);
  not not_2 (not_2_out, B);
  not not_3 (not_3_out, C);
  and doistres (doistres_out, not_1_out, not_2_out, C);
  and cincosete (cincosete_out, not_1_out, B, D);
  and onze (onze_out, not_2_out, C, D);
  and treze (treze_out, B, not_3_out, D);
  or or_1 (Primo, doistres_out, cincosete_out, onze_out, treze_out);
endmodule
